// Logisim project sumadorDe4bit.circ as structural Verilog: 1 circuit, main circuit main
module main (
  input  CARRY,
  input  A,
  input  B,
  output carry_2,
  output suma
);

  wire acarreo_inicial_out, suma_A_B_out, suma_si_crea_acarreo_y_el_anteior_out;

  and acarreo_inicial (acarreo_inicial_out, A, B);
  xor suma_A_B (suma_A_B_out, A, B);
  and suma_si_crea_acarreo_y_el_anteior (suma_si_crea_acarreo_y_el_anteior_out, suma_A_B_out, CARRY);
  xor suma_del_acarreo_anterior (suma, suma_A_B_out, CARRY);
  or or_1 (carry_2, acarreo_inicial_out, suma_si_crea_acarreo_y_el_anteior_out);
endmodule
